// Logisim project project.circ as structural Verilog
module main (
  input  addr_valid,
  input  [7:0] data_in,
  input  we,
  input  clk,
  input  reset,
  input  re
);

  wire algum_ativo, ALUSrc, and_5_out, and_6_out, and_9_out, and_10_out, AUIPC, Branch, branch_taken,
       button_1_out, button_2_out, clock_1_out, comparator_2_gt, comparator_3_eq, comparator_3_lt,
       comparator_5_eq, comparator_5_gt, comparator_6_lt, comparator_7_eq, comparator_8_eq, comparator_8_gt,
       comparator_9_lt, comparator_10_eq, INPUT_cS, Lt, multiplexer_2_out, nenhum_ativo, not_2_out,
       not_3_out, not_4_out, or_1_out, or_2_out, or_6_out, ram_1_p2, ram_1_p7, RAM_CS, RAM_WE, ROM_CS,
       t_ff_1_q, VIDEO_CS, VIDEO_WE, zero;
  wire [1:0] or_4_out;
  wire [2:0] funct3;
  wire [3:0] ALUop, ram_1_p3, UP_out, x, y;
  wire [7:0] datamem_1_write_data_out, datamem_1_write_data_out_2, datamem_1_write_data_out_3,
       datamem_1_write_data_out_4, undriven, undriven_2, undriven_3, undriven_4;
  wire [11:0] control_word;
  wire [15:0] ram_1_p1;
  wire [31:0] addr, alu_result, bit_extender_1_out, DATA_IN_t, DATA_OUT, imm_b, imm_i, imm_j, imm_out,
       instruction, pc_1_pc_out, PC_plus_4, ram_read_data, rs1_val, rs2_val, subtractor_1_out;
  wire [31:8] shifter_1_out;

  PC pc_1 (
    .branch_taken(branch_taken), .jump(control_word[4]), .jalr(control_word[3]), .imm_b(imm_b),
    .imm_j(imm_j), .clk(clk), .reset(reset), .rs1_val(rs1_val), .imm_i(imm_i), .pc_out(pc_1_pc_out),
    .pc_plus_4(PC_plus_4));
  Comparator #(.width(32)) comparator_1 (.a(addr), .b(32'h2000), .gt(ROM_CS));  // open: eq, lt
  Comparator #(.width(32)) comparator_2 (.a(addr), .b(32'h400), .gt(comparator_2_gt));  // open: eq, lt
  Comparator #(.width(32)) comparator_3 (
    .a(addr), .b(32'h800), .eq(comparator_3_eq), .lt(comparator_3_lt));  // open: gt
  Comparator #(.width(32)) comparator_4 (.a(addr), .b(32'h900), .eq(INPUT_cS));  // open: gt, lt
  Comparator #(.width(32)) comparator_5 (
    .a(addr), .b(32'h1000), .gt(comparator_5_gt), .eq(comparator_5_eq));  // open: lt
  Comparator #(.width(32)) comparator_6 (.a(addr), .b(32'h3000), .lt(comparator_6_lt));  // open: gt, eq
  and and_1 (VIDEO_WE, control_word[9], VIDEO_CS);
  and and_2 (RAM_WE, control_word[9], RAM_CS);
  CU cu_1 (
    .instruction({instruction[31:15], funct3, instruction[11:0]}),
    .control_word({AUIPC, control_word[11:7], ALUSrc, Branch, control_word[4:0]}), .ALUop(ALUop));
  or or_1 (or_1_out, comparator_3_eq, comparator_3_lt);
  or or_2 (or_2_out, comparator_5_gt, comparator_5_eq);
  ROM #(.addrWidth(16), .dataWidth(32)) InstMem (
    .addr(pc_1_pc_out[17:2]), .data({instruction[31:15], funct3, instruction[11:0]}));
  and and_3 (VIDEO_CS, comparator_2_gt, or_1_out);
  and and_4 (RAM_CS, or_2_out, comparator_6_lt);
  // Probe on funct3
  or or_3 (algum_ativo, ROM_CS, RAM_CS, INPUT_cS);
  not not_1 (nenhum_ativo, algum_ativo);
  not not_2 (not_2_out, zero);
  not not_3 (not_3_out, Lt);
  // Probe on ram_1_p1
  // Probe on {datamem_1_write_data_out_4, datamem_1_write_data_out_3, datamem_1_write_data_out_2, datamem_1_write_data_out}
  Comparator #(.width(32)) comparator_7 (.a(alu_result), .b(32'hc), .eq(comparator_7_eq));  // open: gt, lt
  or or_4 (or_4_out[0], RAM_CS, nenhum_ativo);
  or or_5 (or_4_out[1], INPUT_cS, nenhum_ativo);
  // RAM #(.addrWidth(16), .clearpin("true"), .enables("line"), .line("quad")) ram_1: pin names not known; wires that end beside it: ram_1_p1, ram_1_p2, ram_1_p3[0], ram_1_p3[1], ram_1_p3[2], ram_1_p3[3], ram_1_p7
  and and_5 (and_5_out, comparator_7_eq, control_word[9]);
  Clock clock_1 (.out(clock_1_out));
  T_Flip_Flop t_ff_1 (.T(button_1_out), .clk(button_1_out), .Q(t_ff_1_q));  // open: Qn, reset, preset
  Button button_1 (.out(button_1_out));
  Button LEFT (.out(UP_out[1]));
  Button RIGHT (.out(UP_out[2]));
  Multiplexer #(.select(2), .width(32)) multiplexer_1 (
    .in0({instruction[31:15], funct3, instruction[11:0]}), .in1(DATA_OUT), .in2(DATA_OUT), .in3({32{1'b0}}),
    .out(DATA_IN_t), .sel(or_4_out));
  Multiplexer #(.select(3)) multiplexer_2 (
    .in0(zero), .in1(not_2_out), .in2(1'b0), .in3(1'b0), .in4(Lt), .in5(not_3_out), .in6(1'b0), .in7(1'b0),
    .out(multiplexer_2_out), .sel(funct3));
  not not_4 (not_4_out, and_5_out);
  and and_6 (and_6_out, not_4_out, clock_1_out);
  Multiplexer multiplexer_3 (.in0(and_6_out), .in1(button_2_out), .out(clk), .sel(t_ff_1_q));
  Button button_2 (.out(button_2_out));
  Button UP (.out(UP_out[0]));
  Button DOWN (.out(UP_out[3]));
  and and_7 (branch_taken, multiplexer_2_out, Branch);
  DataMem datamem_1 (
    .Reset({reset, 1'bz}), .raw({undriven_4, undriven_3, undriven_2, undriven}), .ck({clk, ram_1_p7}),
    .funct3(funct3), .write_data(rs2_val), .mw({control_word[9], ram_1_p2}), .addr_in(alu_result),
    .write_data_out({datamem_1_write_data_out_4, datamem_1_write_data_out_3, datamem_1_write_data_out_2, datamem_1_write_data_out}),
    .raw_read_data(DATA_OUT), .read_data(ram_read_data), .lm(ram_1_p3), .addr(ram_1_p1));
  // AND_Gate and_8 is placed but not wired
  Comparator #(.width(32)) comparator_8 (
    .a(addr), .b(32'h400), .gt(comparator_8_gt), .eq(comparator_8_eq));  // open: lt
  Comparator #(.width(32)) comparator_9 (.a(addr), .b(32'h800), .lt(comparator_9_lt));  // open: gt, eq
  Subtractor #(.width(32)) subtractor_1 (.a(addr), .b(32'h400), .out(subtractor_1_out));  // open: bin, bout
  // Probe on alu_result
  or or_6 (or_6_out, comparator_8_gt, comparator_8_eq);
  Shifter #(.shift("lr"), .width(32)) shifter_1 (.in(subtractor_1_out), .\dist (5'b00010), .out({shifter_1_out, y, x}));
  assign bit_extender_1_out = {{28{UP_out[3]}}, UP_out};  // Bit_Extender bit_extender_1
  Button button_3 (.out(reset));
  buf and_9 (and_9_out, comparator_9_lt);  // AND_Gate
  Comparator #(.width(32)) comparator_10 (.a(addr), .b(32'h900), .eq(comparator_10_eq));  // open: gt, lt
  // Probe on imm_out
  ImmGen immgen_1 (
    .imm_sel(control_word[2:0]), .instr({instruction[31:15], funct3, instruction[11:0]}), .type_b(imm_b),
    .type_i(imm_i), .type_j(imm_j), .imm_out(imm_out));
  // RGB_Video #(.height(16), .scale(8), .width(16)) rgb_video_1: pin names not known; wires that end beside it: or_6_out, and_9_out, addr_valid, reset, clk, we, x, y, data_in
  and and_10 (and_10_out, comparator_10_eq, re);
  // Probe on {AUIPC, control_word[11:7], ALUSrc, Branch, control_word[4:0]}
  // Probe on instruction[11:7]
  // Probe on control_word[8:7]
  RegFile regfile_1 (
    .rs2_index(instruction[24:20]), .rs1_index(instruction[19:15]), .ram_read_data(ram_read_data),
    .Pc_plus_4(PC_plus_4), .RegWrite(control_word[11]), .Reset(reset), .alu_result(alu_result),
    .rd_index(instruction[11:7]), .clk(clk), .MemtoReg(control_word[8:7]), .rs2_data(rs2_val),
    .rs1_data(rs1_val));
  Multiplexer #(.width(32)) multiplexer_4 (
    .in0({32{1'b0}}), .in1(bit_extender_1_out), .out(DATA_OUT), .sel(and_10_out));
  ALU alu_1 (
    .ALUop(ALUop), .PC_plus_4(PC_plus_4), .rs1_val(rs1_val), .AUIPC(AUIPC), .ALUSrc(ALUSrc),
    .imm_out(imm_out), .rs2_val(rs2_val), .Result(alu_result), .zero(zero), .Lt(Lt));  // open: Ltu

  // Other names for the same wires on the sheet: immSel[2:0] = control_word[2:0]; jalr = control_word[3];
  //   jal = control_word[4]; control_word (some bits) = {AUIPC, ALUSrc, Branch}; MemToReg[1:0] = control_word[8:7];
  //   MemWrite = control_word[9]; MemRead = control_word[10]; RegWrite = control_word[11];
  //   rd_index[4:0] = instruction[11:7]; instruction[14:12] = funct3; rs1_index[4:0] = instruction[19:15];
  //   rs2_index[4:0] = instruction[24:20]; RAM_OUT[31:0] = DATA_OUT

  // Notes on the sheet:
  //   data_in: initial=0x9
  //   contents of InstMem (hex, n*v repeats v):
  //   10137 10113 2b7 68028293 1337 89430313 628863 2a023 428293 ff5ff06f 5ec000ef 6f 58c63 b57663 8067
  //   40b50533 feb57ee3 8067 58513 8067 637 67c62703 871693 40e686b3 369793 e787b3 779693 e686b3 369793
  //   40e787b3 579693 d787b3 279693 40e687b3 279513 e50533 37b7 3978793 f50533 800007b7 fff78793 f57533
  //   66a62e23 8067 ff010113 12623 140006f 13 c12783 178793 f12623 c12783 fea7e6e3 1010113 8067 ff010113
  //   112623 812423 713 200006f 171693 7b7 68078793 d787b3 78023 780a3 170713 ff00793 fee7d0e3 7b7
  //   68078793 800713 e78023 e780a3 300713 20e7a023 100793 2c0006f 737 68070713 74603 40f60633 179693
  //   d706b3 c68023 174703 e680a3 178793 200713 fcf77ae3 437 68040413 100793 20f42223 97 ed8080e7 e00593
  //   97 eac080e7 150793 20f40423 97 ebc080e7 e00593 97 e90080e7 150793 20f404a3 20042623 20042823 c12083
  //   812403 1010113 8067 100713 80006f 170713 7b7 68078793 2007a783 2f77c63 171693 7b7 68078793 d787b3
  //   7c783 fca79ce3 7b7 68078793 d787b3 17c783 fcb792e3 100513 8067 513 8067 f00793 a7e863 b7fa63 100513
  //   8067 100513 8067 513 8067 ff010113 112623 812423 912223 413 540006f 170713 7b7 68078793 2007a783
  //   2f77e63 7b7 68078793 171693 d786b3 6c683 2087c783 fcf69ae3 171693 7b7 68078793 d787b3 17c783
  //   faf51ee3 80006f 100413 4041863 97 da0080e7 e00593 97 d74080e7 150513 4b7 68048493 20a48423 97
  //   d7c080e7 e00593 97 d50080e7 150513 ff57513 20a484a3 713 f69ff06f c12083 812403 412483 1010113 8067
  //   50002503 f57513 8067 7b7 68078793 2107a783 78463 8067 ff010113 112623 812423 912223 97 fd0080e7
  //   157793 4078e63 7b7 68078793 2047a703 200793 4f70463 7b7 68078793 2007a223 7b7 68078793 7c403 17c483
  //   2047a783 200713 10e78263 af76463 a078c63 100713 ae79c63 140413 ff47413 ac0006f 257793 2078663 7b7
  //   68078793 2047a703 300793 f70c63 7b7 68078793 100713 20e7a223 f9dff06f 457793 2078463 7b7 68078793
  //   2047a783 78c63 7b7 68078793 200713 20e7a223 f71ff06f 857513 f60504e3 7b7 68078793 2047a703 100793
  //   f4f70ae3 7b7 68078793 300713 20e7a223 f41ff06f 300713 e79c63 fff40413 ff47413 c0006f fff48493
  //   ff4f493 48593 40513 97 dc8080e7 2051c63 48593 40513 97 d5c080e7 2051263 7b7 68078793 2007a583
  //   fff58793 5c0006f 148493 ff4f493 fbdff06f 7b7 68078793 100713 20e7a823 c12083 812403 412483 1010113
  //   8067 fff78693 737 68070713 179793 f707b3 169613 c70733 75703 e79023 68793 fcf04ce3 7b7 68078793
  //   878023 9780a3 2087c783 fa8796e3 7b7 68078793 2097c783 f8979ee3 ff00793 2b7e063 7b7 68078793 158593
  //   20b7a023 20c7a703 a70713 20e7a623 97 d10080e7 f6dff06f 793 100006f 279713 40072023 178793 f00713
  //   fef758e3 713 80006f 170713 7b7 68078793 2007a783 4f77263 171693 7b7 68078793 d787b3 7c683 17c783
  //   f00613 fcd668e3 fcf666e3 279793 4007a603 100593 d596b3 d666b3 40d7a023 fb1ff06f 7b7 68078793
  //   2087c783 f00713 2f76863 737 68070713 20974703 f00693 e6ee63 271713 40072683 100613 f617b3 f6e7b3
  //   40f72023 7b7 68078793 20c7a703 44e02023 2107a783 44f02223 8067 ff010113 112623 97 ac0080e7 97
  //   cf8080e7 97 f14080e7 c537 35050513 97 a74080e7 7b7 68078793 2107a783 fc078ae3 31537 d4050513 97
  //   a54080e7 97 cac080e7 fa050ce3 97 a6c080e7 fadff06f 3039
  //   buttons
  //   Control Word
  //   bit 11 (RegWrite)
  //   bit 10 (MemRead)
  //   bit 9 (MemWrite)
  //   bits 8..7 (MemToReg[1:0])
  //   bit 6 (ALUSrc)
  //   bit 5 (Branch)
  //   bit 4 (Jump(JAL))
  //   bit 3 (Jalr)
  //   bits 2..0 (ImmSel[2:0])
endmodule

module PC (
  input  [31:0] imm_b,
  input  [31:0] imm_j,
  input  [31:0] rs1_val,
  input  clk,
  input  [31:0] imm_i,
  input  reset,
  input  branch_taken,
  input  jump,
  input  jalr,
  output [31:0] pc_out,
  output [31:0] pc_plus_4
);

  wire [31:0] adder_1_out, adder_3_out, adder_4_out, and_1_out, multiplexer_1_out, multiplexer_2_out,
       multiplexer_3_out;

  Register #(.width(32)) pc_reg (.D(multiplexer_3_out), .en(1'b1), .clk(clk), .Q(pc_out), .clr(reset));
  Adder #(.width(32)) adder_1 (.a(rs1_val), .b(imm_i), .out(adder_1_out));  // open: cin, cout
  Adder #(.width(32)) adder_2 (.a(pc_out), .b(32'h4), .out(pc_plus_4));  // open: cin, cout
  Adder #(.width(32)) adder_3 (.a(pc_out), .b(imm_b), .out(adder_3_out));  // open: cin, cout
  Adder #(.width(32)) adder_4 (.a(pc_out), .b(imm_j), .out(adder_4_out));  // open: cin, cout
  assign and_1_out = adder_1_out & 32'hfffffffe;  // AND_Gate and_1, 32 bits wide
  Multiplexer #(.width(32)) multiplexer_1 (
    .in0(pc_plus_4), .in1(adder_3_out), .out(multiplexer_1_out), .sel(branch_taken));
  Multiplexer #(.width(32)) multiplexer_2 (
    .in0(multiplexer_1_out), .in1(adder_4_out), .out(multiplexer_2_out), .sel(jump));
  Multiplexer #(.width(32)) multiplexer_3 (
    .in0(multiplexer_2_out), .in1(and_1_out), .out(multiplexer_3_out), .sel(jalr));

  // Notes on the sheet:
  //   pc_next
endmodule

module InstMem (
  input  [7:0] in_1,
  output [31:0] out_2
);

  ROM #(.dataWidth(32)) rom_1 (.addr(in_1), .data(out_2));

  // Notes on the sheet:
  //   contents of rom_1 (hex, n*v repeats v):
  //   500093 a00113 2081b3 302023 2203
endmodule

module ImmGen (
  input  [31:0] instr,
  input  [2:0] imm_sel,
  output [31:0] type_i,
  output [31:0] imm_out,
  output [31:0] type_b,
  output [31:0] type_j
);

  wire [31:0] bit_extender_1_out;

  assign bit_extender_1_out = {{20{instr[31]}}, {instr[31:25], instr[11:7]}};  // Bit_Extender bit_extender_1
  assign type_i = {{20{instr[31]}}, instr[31:20]};  // Bit_Extender bit_extender_2
  assign type_b = {{19{instr[31]}}, {instr[31], instr[7], instr[30:25], instr[11:8], 1'b0}};  // Bit_Extender bit_extender_3
  assign type_j = {{11{instr[31]}}, {instr[31], instr[19:12], instr[20], instr[30:21], 1'b0}};  // Bit_Extender bit_extender_4
  Multiplexer #(.select(3), .width(32)) multiplexer_1 (
    .in0(type_i), .in1(bit_extender_1_out), .in2(type_b), .in3({instr[31:12], {12{1'b0}}}), .in4(type_j),
    .out(imm_out), .sel(imm_sel));  // open: in5, in6, in7

  // Other names for the same wires on the sheet: p11_8[3:0] = instr[11:8]; p7 = instr[7]; p30_21[9:0] = instr[30:21];
  //   p31_12[19:0] = instr[31:12]; p30_25[5:0] = instr[30:25]; p20 = instr[20]; p19_12[7:0] = instr[19:12];
  //   p31 = instr[31]; p0 = instr[0]

  // Notes on the sheet:
  //   type-s
  //   type-i
  //   type-B
  //   type-u
  //   type-j
endmodule

module RegFile (
  input  [31:0] alu_result,
  input  [31:0] ram_read_data,
  input  [31:0] Pc_plus_4,
  input  [1:0] MemtoReg,
  input  clk,
  input  RegWrite,
  input  Reset,
  input  [4:0] rd_index,
  input  [4:0] rs1_index,
  input  [4:0] rs2_index,
  output [31:0] rs1_data,
  output [31:0] rs2_data
);

  wire demultiplexer_1_out0, demultiplexer_1_out1, demultiplexer_1_out2, demultiplexer_1_out3;
  wire [7:0] demultiplexer_2_out0, demultiplexer_3_out0, demultiplexer_4_out0, demultiplexer_5_out0;
  wire [31:0] write_data, x1_ra_q, x2_sp_q, x3_gp_q, x4_tp_q, x5_t0_q, x6_t1_q, x7_t2_q, x8_s0_q, x9_s1_q,
       x10_a0_q, x11_a1_q, x12_a2_q, x13_a3_q, x14_a4_q, x15_a5_q, x16_a6_q, x17_a7_q, x18_s2_q, x19_s3_q,
       x20_s4_q, x21_s5_q, x22_s6_q, x23_s7_q, x24_s8_q, x25_s9_q, x26_s10_q, x27_s11_q, x28_t3_q, x29_t4_q,
       x30_t5_q, x31_t6_q;

  Demultiplexer #(.select(2)) demultiplexer_1 (
    .out0(demultiplexer_1_out0), .out1(demultiplexer_1_out1), .out2(demultiplexer_1_out2),
    .out3(demultiplexer_1_out3), .in(RegWrite), .sel(rd_index[4:3]));
  Multiplexer #(.select(2), .width(32)) multiplexer_1 (
    .in0(alu_result), .in1(ram_read_data), .in2(Pc_plus_4), .in3({32{1'b0}}), .out(write_data), .sel(MemtoReg));
  // Probe on write_data
  Demultiplexer #(.select(3)) demultiplexer_2 (
    .out0(demultiplexer_2_out0[0]), .out1(demultiplexer_2_out0[1]), .out2(demultiplexer_2_out0[2]),
    .out3(demultiplexer_2_out0[3]), .out4(demultiplexer_2_out0[4]), .out5(demultiplexer_2_out0[5]),
    .out6(demultiplexer_2_out0[6]), .out7(demultiplexer_2_out0[7]), .in(demultiplexer_1_out0),
    .sel(rd_index[2:0]));
  Demultiplexer #(.select(3)) demultiplexer_3 (
    .out0(demultiplexer_3_out0[0]), .out1(demultiplexer_3_out0[1]), .out2(demultiplexer_3_out0[2]),
    .out3(demultiplexer_3_out0[3]), .out4(demultiplexer_3_out0[4]), .out5(demultiplexer_3_out0[5]),
    .out6(demultiplexer_3_out0[6]), .out7(demultiplexer_3_out0[7]), .in(demultiplexer_1_out1),
    .sel(rd_index[2:0]));
  Demultiplexer #(.select(3)) demultiplexer_4 (
    .out0(demultiplexer_4_out0[0]), .out1(demultiplexer_4_out0[1]), .out2(demultiplexer_4_out0[2]),
    .out3(demultiplexer_4_out0[3]), .out4(demultiplexer_4_out0[4]), .out5(demultiplexer_4_out0[5]),
    .out6(demultiplexer_4_out0[6]), .out7(demultiplexer_4_out0[7]), .in(demultiplexer_1_out2),
    .sel(rd_index[2:0]));
  Demultiplexer #(.select(3)) demultiplexer_5 (
    .out0(demultiplexer_5_out0[0]), .out1(demultiplexer_5_out0[1]), .out2(demultiplexer_5_out0[2]),
    .out3(demultiplexer_5_out0[3]), .out4(demultiplexer_5_out0[4]), .out5(demultiplexer_5_out0[5]),
    .out6(demultiplexer_5_out0[6]), .out7(demultiplexer_5_out0[7]), .in(demultiplexer_1_out3),
    .sel(rd_index[2:0]));
  Register #(.width(32)) x8_s0 (.D(write_data), .en(demultiplexer_3_out0[0]), .clk(clk), .Q(x8_s0_q), .clr(Reset));
  Register #(.width(32)) x16_a6 (.D(write_data), .en(demultiplexer_4_out0[0]), .clk(clk), .Q(x16_a6_q), .clr(Reset));
  Register #(.width(32)) x24_s8 (.D(write_data), .en(demultiplexer_5_out0[0]), .clk(clk), .Q(x24_s8_q), .clr(Reset));
  Register #(.width(32)) x1_ra (.D(write_data), .en(demultiplexer_2_out0[1]), .clk(clk), .Q(x1_ra_q), .clr(Reset));
  Register #(.width(32)) x9_s1 (.D(write_data), .en(demultiplexer_3_out0[1]), .clk(clk), .Q(x9_s1_q), .clr(Reset));
  Register #(.width(32)) x17_a7 (.D(write_data), .en(demultiplexer_4_out0[1]), .clk(clk), .Q(x17_a7_q), .clr(Reset));
  Register #(.width(32)) x25_s9 (.D(write_data), .en(demultiplexer_5_out0[1]), .clk(clk), .Q(x25_s9_q), .clr(Reset));
  Register #(.width(32)) x2_sp (.D(write_data), .en(demultiplexer_2_out0[2]), .clk(clk), .Q(x2_sp_q), .clr(Reset));
  Register #(.width(32)) x10_a0 (.D(write_data), .en(demultiplexer_3_out0[2]), .clk(clk), .Q(x10_a0_q), .clr(Reset));
  Register #(.width(32)) x18_s2 (.D(write_data), .en(demultiplexer_4_out0[2]), .clk(clk), .Q(x18_s2_q), .clr(Reset));
  Register #(.width(32)) x26_s10 (.D(write_data), .en(demultiplexer_5_out0[2]), .clk(clk), .Q(x26_s10_q), .clr(Reset));
  Register #(.width(32)) x3_gp (.D(write_data), .en(demultiplexer_2_out0[3]), .clk(clk), .Q(x3_gp_q), .clr(Reset));
  Register #(.width(32)) x11_a1 (.D(write_data), .en(demultiplexer_3_out0[3]), .clk(clk), .Q(x11_a1_q), .clr(Reset));
  Register #(.width(32)) x19_s3 (.D(write_data), .en(demultiplexer_4_out0[3]), .clk(clk), .Q(x19_s3_q), .clr(Reset));
  Register #(.width(32)) x27_s11 (.D(write_data), .en(demultiplexer_5_out0[3]), .clk(clk), .Q(x27_s11_q), .clr(Reset));
  Register #(.width(32)) x4_tp (.D(write_data), .en(demultiplexer_2_out0[4]), .clk(clk), .Q(x4_tp_q), .clr(Reset));
  Register #(.width(32)) x12_a2 (.D(write_data), .en(demultiplexer_3_out0[4]), .clk(clk), .Q(x12_a2_q), .clr(Reset));
  Register #(.width(32)) x20_s4 (.D(write_data), .en(demultiplexer_4_out0[4]), .clk(clk), .Q(x20_s4_q), .clr(Reset));
  Register #(.width(32)) x28_t3 (.D(write_data), .en(demultiplexer_5_out0[4]), .clk(clk), .Q(x28_t3_q), .clr(Reset));
  Register #(.width(32)) x5_t0 (.D(write_data), .en(demultiplexer_2_out0[5]), .clk(clk), .Q(x5_t0_q), .clr(Reset));
  Register #(.width(32)) x13_a3 (.D(write_data), .en(demultiplexer_3_out0[5]), .clk(clk), .Q(x13_a3_q), .clr(Reset));
  Register #(.width(32)) x21_s5 (.D(write_data), .en(demultiplexer_4_out0[5]), .clk(clk), .Q(x21_s5_q), .clr(Reset));
  Register #(.width(32)) x29_t4 (.D(write_data), .en(demultiplexer_5_out0[5]), .clk(clk), .Q(x29_t4_q), .clr(Reset));
  Register #(.width(32)) x6_t1 (.D(write_data), .en(demultiplexer_2_out0[6]), .clk(clk), .Q(x6_t1_q), .clr(Reset));
  Register #(.width(32)) x14_a4 (.D(write_data), .en(demultiplexer_3_out0[6]), .clk(clk), .Q(x14_a4_q), .clr(Reset));
  Register #(.width(32)) x22_s6 (.D(write_data), .en(demultiplexer_4_out0[6]), .clk(clk), .Q(x22_s6_q), .clr(Reset));
  Register #(.width(32)) x30_t5 (.D(write_data), .en(demultiplexer_5_out0[6]), .clk(clk), .Q(x30_t5_q), .clr(Reset));
  Register #(.width(32)) x7_t2 (.D(write_data), .en(demultiplexer_2_out0[7]), .clk(clk), .Q(x7_t2_q), .clr(Reset));
  Register #(.width(32)) x15_a5 (.D(write_data), .en(demultiplexer_3_out0[7]), .clk(clk), .Q(x15_a5_q), .clr(Reset));
  Register #(.width(32)) x23_s7 (.D(write_data), .en(demultiplexer_4_out0[7]), .clk(clk), .Q(x23_s7_q), .clr(Reset));
  Register #(.width(32)) x31_t6 (.D(write_data), .en(demultiplexer_5_out0[7]), .clk(clk), .Q(x31_t6_q), .clr(Reset));
  Multiplexer #(.select(5), .width(32)) multiplexer_2 (
    .in0({32{1'b0}}), .in1(x1_ra_q), .in2(x2_sp_q), .in3(x3_gp_q), .in4(x4_tp_q), .in5(x5_t0_q),
    .in6(x6_t1_q), .in7(x7_t2_q), .in8(x8_s0_q), .in9(x9_s1_q), .in10(x10_a0_q), .in11(x11_a1_q),
    .in12(x12_a2_q), .in13(x13_a3_q), .in14(x14_a4_q), .in15(x15_a5_q), .in16(x16_a6_q), .in17(x17_a7_q),
    .in18(x18_s2_q), .in19(x19_s3_q), .in20(x20_s4_q), .in21(x21_s5_q), .in22(x22_s6_q), .in23(x23_s7_q),
    .in24(x24_s8_q), .in25(x25_s9_q), .in26(x26_s10_q), .in27(x27_s11_q), .in28(x28_t3_q), .in29(x29_t4_q),
    .in30(x30_t5_q), .in31(x31_t6_q), .out(rs1_data), .sel(rs1_index));
  Multiplexer #(.select(5), .width(32)) multiplexer_3 (
    .in0({32{1'b0}}), .in1(x1_ra_q), .in2(x2_sp_q), .in3(x3_gp_q), .in4(x4_tp_q), .in5(x5_t0_q),
    .in6(x6_t1_q), .in7(x7_t2_q), .in8(x8_s0_q), .in9(x9_s1_q), .in10(x10_a0_q), .in11(x11_a1_q),
    .in12(x12_a2_q), .in13(x13_a3_q), .in14(x14_a4_q), .in15(x15_a5_q), .in16(x16_a6_q), .in17(x17_a7_q),
    .in18(x18_s2_q), .in19(x19_s3_q), .in20(x20_s4_q), .in21(x21_s5_q), .in22(x22_s6_q), .in23(x23_s7_q),
    .in24(x24_s8_q), .in25(x25_s9_q), .in26(x26_s10_q), .in27(x27_s11_q), .in28(x28_t3_q), .in29(x29_t4_q),
    .in30(x30_t5_q), .in31(x31_t6_q), .out(rs2_data), .sel(rs2_index));

  // Other names for the same wires on the sheet: R = Reset; rd_index2_0[2:0] = rd_index[2:0];
  //   rd_index4_3[1:0] = rd_index[4:3]

  // Notes on the sheet:
  //   x0_zero
endmodule

module ALU (
  input  [31:0] rs1_val,
  input  [31:0] rs2_val,
  input  [31:0] PC_plus_4,
  input  AUIPC,
  input  [31:0] imm_out,
  input  ALUSrc,
  input  [3:0] ALUop,
  output [31:0] Result,
  output zero,
  output Lt,
  output Ltu
);

  wire [31:0] adder_1_out, and_1_out, bit_extender_1_out, bit_extender_2_out, or_1_out, rs1_val_t,
       rs2_or_imm, shifter_1_out, shifter_2_out, shifter_3_out, subtractor_1_out, subtractor_2_out, xor_1_out;

  Subtractor #(.width(32)) subtractor_1 (.a(PC_plus_4), .b(32'h4), .out(subtractor_1_out));  // open: bin, bout
  Multiplexer #(.width(32)) multiplexer_1 (.in0(rs1_val), .in1(subtractor_1_out), .out(rs1_val_t), .sel(AUIPC));
  Multiplexer #(.width(32)) multiplexer_2 (.in0(rs2_val), .in1(imm_out), .out(rs2_or_imm), .sel(ALUSrc));
  Comparator #(.width(32)) comparator_1 (.a(rs1_val_t), .b(rs2_or_imm), .lt(Lt));  // open: gt, eq
  Comparator #(.mode("unsigned"), .width(32)) comparator_2 (.a(rs1_val_t), .b(rs2_or_imm), .lt(Ltu));  // open: gt, eq
  Adder #(.width(32)) adder_1 (.a(rs1_val_t), .b(rs2_or_imm), .out(adder_1_out));  // open: cin, cout
  Subtractor #(.width(32)) subtractor_2 (.a(rs1_val_t), .b(rs2_or_imm), .out(subtractor_2_out));  // open: bin, bout
  Shifter #(.width(32)) shifter_1 (.in(rs1_val_t), .\dist (rs2_or_imm[4:0]), .out(shifter_1_out));
  assign bit_extender_1_out = {{31{1'b0}}, Lt};  // Bit_Extender bit_extender_1
  assign bit_extender_2_out = {{31{1'b0}}, Ltu};  // Bit_Extender bit_extender_2
  assign xor_1_out = rs1_val_t ^ rs2_or_imm;  // XOR_Gate xor_1, 32 bits wide
  Shifter #(.shift("lr"), .width(32)) shifter_2 (.in(rs1_val_t), .\dist (rs2_or_imm[4:0]), .out(shifter_2_out));
  Shifter #(.shift("ar"), .width(32)) shifter_3 (.in(rs1_val_t), .\dist (rs2_or_imm[4:0]), .out(shifter_3_out));
  assign or_1_out = rs1_val_t | rs2_or_imm;  // OR_Gate or_1, 32 bits wide
  assign and_1_out = rs1_val_t & rs2_or_imm;  // AND_Gate and_1, 32 bits wide
  Multiplexer #(.select(4), .width(32)) multiplexer_3 (
    .in0(adder_1_out), .in1(subtractor_2_out), .in2(shifter_1_out), .in3(bit_extender_1_out),
    .in4(bit_extender_2_out), .in5(xor_1_out), .in6(shifter_2_out), .in7(shifter_3_out), .in8(or_1_out),
    .in9(and_1_out), .in10(rs2_or_imm), .in11(rs1_val_t), .out(Result), .sel(ALUop));  // open: in12, in13, in14, in15
  Comparator #(.width(32)) comparator_3 (.a(Result), .b({32{1'b0}}), .eq(zero));  // open: gt, lt

  // Other names for the same wires on the sheet: shamt[4:0] = rs2_or_imm[4:0]

  // Notes on the sheet:
  //   SLT-0011
  //   SLTU-0100
  //   XOR-0101
  //   SRL-0110
  //   SRA-0111
  //   OR-1000
  //   AND-1001
  //   COPY-B-1010
  //   PASS-A-1011
  //   ADD-0000
  //   SUB-0001
  //   SLL-0010
endmodule

module CU (
  input  [31:0] instruction,
  output [12:0] control_word,
  output [3:0] ALUop
);

  // Probe on instruction[6:0]
  // Probe on instruction[14:12]
  // Probe on instruction[30]
  // Probe on instruction[6:0]
  ROM #(.addrWidth(11), .dataWidth(17)) rom_1 (
    .addr({instruction[30], instruction[14:12], instruction[6:0]}), .data({control_word, ALUop}));
  // Probe on {instruction[30], instruction[14:12], instruction[6:0]}

  // Other names for the same wires on the sheet: opcode[6:0] = instruction[6:0]; funct3[2:0] = instruction[14:12];
  //   funct7_bit = instruction[30]

  // Notes on the sheet:
  //   contents of rom_1 (hex, n*v repeats v):
  //   0 0 0 cc00 15*0 8400 0 0 0 18431 11*0 2410 15*0 8000 0 0 0 8430 43*0 231 0 0 0 9481 7*0 9140 19*0
  //   cc00 15*0 8402 0 0 0 18432 11*0 2410 15*0 8002 0 0 0 8430 43*0 231 0 0 0 9482 7*0 9142 19*0 cc00
  //   15*0 8403 0 0 0 18433 11*0 2410 15*0 8003 0 0 0 8430 43*0 2233 0 0 0 9483 7*0 9140 19*0 cc00 15*0
  //   8403 0 0 0 18434 11*0 2410 15*0 8003 0 0 0 8430 43*0 2234 0 0 0 9484 7*0 9144 19*0 cc00 15*0 8400 0
  //   0 0 18435 11*0 2410 15*0 8005 0 0 0 8430 43*0 233 0 0 0 9485 7*0 9145 19*0 cc00 15*0 8406 0 0 0
  //   18436 11*0 2410 15*0 8006 0 0 0 8430 43*0 231 0 0 0 9486 7*0 9146 19*0 cc01 15*0 8400 0 0 0 18438
  //   11*0 2411 15*0 8008 0 0 0 8431 43*0 2238 0 0 0 9488 7*0 9148 19*0 cc01 15*0 8409 0 0 0 18439 11*0
  //   2411 15*0 8009 0 0 0 8431 43*0 231 0 0 0 9489 7*0 9149 19*0 cc01 15*0 8400 0 0 0 18431 11*0 2411
  //   15*0 8001 0 0 0 8431 43*0 2231 0 0 0 9481 7*0 9141 19*0 cc01 15*0 8400 0 0 0 18432 11*0 2411 15*0
  //   8000 0 0 0 8431 43*0 231 0 0 0 9482 7*0 9142 19*0 cc01 15*0 8400 0 0 0 18433 11*0 2411 15*0 8000 0 0
  //   0 8431 43*0 2233 0 0 0 9483 7*0 9143 19*0 cc01 15*0 8400 0 0 0 18434 11*0 2411 15*0 8000 0 0 0 8431
  //   43*0 2234 0 0 0 9484 7*0 9144 19*0 cc01 15*0 8400 0 0 0 18435 11*0 2411 15*0 8000 0 0 0 8431 43*0
  //   231 0 0 0 9485 7*0 9145 19*0 cc01 15*0 8407 0 0 0 18437 11*0 2411 15*0 8007 0 0 0 8431 43*0 237 0 0
  //   0 9487 7*0 9147 19*0 cc01 15*0 8400 0 0 0 18438 11*0 2411 15*0 8000 0 0 0 8431 43*0 2238 0 0 0 9488
  //   7*0 9148 19*0 cc01 15*0 8400 0 0 0 18439 11*0 2411 15*0 8000 0 0 0 8431 43*0 231 0 0 0 9489 7*0 9149
endmodule

module DataMem (
  input  [31:0] addr_in,
  input  Reset,
  input  clk,
  input  [31:0] raw,
  input  MemWrite,
  input  [2:0] funct3,
  input  [31:0] write_data,
  output R,
  output ck,
  output [15:0] addr,
  output [31:0] raw_read_data,
  output mw,
  output [31:0] read_data,
  output [3:0] lm,
  output [31:0] write_data_out
);

  wire [3:0] sb_mask, sh_mask;
  wire [4:0] bit_extender_1_out, shift_amt;
  wire [31:0] LB, LBU, LH, LHU, mid_result, shifter_3_out, shifter_4_out, shifter_5_out;

  Multiplexer #(.select(2), .width(4)) multiplexer_1 (
    .in0(4'b0001), .in1(4'b0010), .in2(4'b0100), .in3(4'b1000), .out(sb_mask), .sel(addr_in[1:0]));
  Multiplexer #(.select(2), .width(4)) multiplexer_2 (
    .in0(4'b0011), .in2(4'b1100), .out(sh_mask), .sel(addr_in[1:0]));  // open: in1, in3
  Multiplexer #(.select(3), .width(4)) multiplexer_3 (
    .in0(sb_mask), .in1(sh_mask), .in2(4'b1111), .out(lm), .sel(funct3));  // open: in3, in4, in5, in6, in7
  Shifter #(.width(32)) shifter_1 (.in(write_data), .\dist (shift_amt), .out(mid_result));
  Multiplexer #(.select(3), .width(32)) multiplexer_4 (
    .in0(mid_result), .in1(mid_result), .in2(write_data), .out(write_data_out), .sel(funct3));  // open: in3, in4, in5, in6, in7
  assign bit_extender_1_out = {{3{1'b0}}, addr_in[1:0]};  // Bit_Extender bit_extender_1
  Shifter #(.width(5)) shifter_2 (.in(bit_extender_1_out), .\dist (3'b011), .out(shift_amt));
  Shifter #(.shift("lr"), .width(32)) shifter_3 (.in(raw), .\dist (shift_amt), .out(shifter_3_out));
  Shifter #(.width(32)) shifter_4 (.in(LBU), .\dist (5'b11000), .out(shifter_4_out));
  Shifter #(.width(32)) shifter_5 (.in(LHU), .\dist (5'b10000), .out(shifter_5_out));
  assign LBU = 32'hff & shifter_3_out;  // AND_Gate and_1, 32 bits wide
  assign LHU = 32'hffff & shifter_3_out;  // AND_Gate and_2, 32 bits wide
  Shifter #(.shift("ar"), .width(32)) shifter_6 (.in(shifter_4_out), .\dist (5'b11000), .out(LB));
  Shifter #(.shift("ar"), .width(32)) shifter_7 (.in(shifter_5_out), .\dist (5'b10000), .out(LH));
  Multiplexer #(.select(3), .width(32)) multiplexer_5 (
    .in0(LB), .in1(LH), .in2(raw), .in3({32{1'b0}}), .in4(LBU), .in5(LHU), .in6({32{1'b0}}),
    .in7({32{1'b0}}), .out(read_data), .sel(funct3));

  assign addr = {addr_in[15:2], 2'b00};
  assign ck = clk;
  assign mw = MemWrite;
  assign R = Reset;
  assign raw_read_data = raw;

  // Other names for the same wires on the sheet: offset[1:0] = addr_in[1:0]; f3[2:0] = funct3; LW[31:0] = raw
endmodule

module parser (
);

  wire AUIPC, button_1_out, clk, comparator_1_eq, funct7_bit;
  wire [2:0] funct3;
  wire [3:0] ALUop;
  wire [5:4] word_data;
  wire [6:0] opcode;
  wire [11:0] controlword;
  wire [16:0] multiplexer_1_out, ram_1_dout;

  Button button_1 (.out(button_1_out));
  Clock clock_1 (.out(clk));
  Counter #(.max('h7ff), .ongoal("stay"), .width(11)) counter_1 (
    .clr(button_1_out), .up(1'b1), .count(1'b1), .clk(clk), .Q({funct7_bit, funct3, opcode}));  // open: load, D, carry
  Comparator #(.width(12)) comparator_1 (.a(controlword), .b({12{1'b0}}), .eq(comparator_1_eq));  // open: gt, lt
  Multiplexer #(.width(17)) multiplexer_1 (
    .in0({AUIPC, controlword, ALUop}), .in1({17{1'b0}}), .out(multiplexer_1_out), .sel(comparator_1_eq));
  Comparator #(.width(7)) comparator_2 (.a(opcode), .b(7'b0010111), .eq(AUIPC));  // open: gt, lt
  RAM #(.addrWidth(11), .asyncread("true"), .dataWidth(17)) ram_1 (
    .addr({funct7_bit, funct3, opcode}), .we(1'b1), .oe(1'b1), .clk(clk), .din(multiplexer_1_out),
    .dout(ram_1_dout));
  ROM #(.addrWidth(7), .dataWidth(14)) word (.addr(opcode), .data({controlword, word_data}));
  // Probe on ram_1_dout
  // Probe on controlword
  ROM #(.addrWidth(6), .dataWidth(4)) ALUControl (.addr({word_data, funct7_bit, funct3}), .data(ALUop));

  // Notes on the sheet:
  //   contents of word (hex, n*v repeats v):
  //   0 0 0 3302 15*0 2103 0 0 0 210c 11*0 906 15*0 2003 0 0 0 210e 43*0 88c 0 0 0 2520 7*0 2451
  //   contents of ALUControl (hex, n*v repeats v):
  //   1 2 3 4 5 6 8 9 1 2 3 4 5 7 8 9 0 2 0 4 5 6 8 9 1 2 3 4 5 7 8 9 6*0 10*1 0 2 3 3 0 6 0 9 5*0 7
endmodule

module test (
);

  // RGB_Video rgb_video_1: pin names not known
endmodule
